# Fritzing sketch desafio4 (saved by Fritzing 0.9.3b)
breadboards: 2

parts:
  U1 = ESP8266 NodeMCU LoLin module
  LED1 = LED - 5mm [color="Red (633nm)" package="5 mm [THT]"]
  Part1 = HC-SR501 Body Sensor Module

nets:
  N1: U1.D2, Part1.OUT
  3V3: U1.3V3, Part1.VCC
  GND: U1.GND, LED1.cathode, Part1.GND
  N2: U1.D8, LED1.anode

notes:
  VCC
  GND
  OUT

custom parts:
  ESP8266 NodeMCU LoLin module: ESP8266 based NodeMCU
  HC-SR501 Body Sensor Module: Pyroelectric Infrared PIR Motion Sensor Detector Module
