# Fritzing sketch desafio5 (saved by Fritzing 0.9.3b)
breadboards: 2

parts:
  U1 = ESP8266 NodeMCU LoLin module
  KY-1 = Keyes Relay [package=THT]

nets:
  N1: U1.GND, KY-1.ground
  N2: U1.D8, KY-1.signal
  N3: U1.Vin, KY-1.power

custom parts:
  ESP8266 NodeMCU LoLin module: ESP8266 based NodeMCU
  Keyes Relay: The Keyes 5V relay module is suitable for SCM development, home appliance control. It uses a 5V~12V TIL control signal which can control DC / AC signal.
